# Fritzing sketch blue_pill_rs-485 (saved by Fritzing 1.0.1rc)
breadboards: 1

parts:
  M1 = STM32F103C8T6 blue mini board
  U1 = MAX485 [package=dil08]
  R1 = Resistor [tolerance=±5% resistance=100 package="0805 [SMD]"]
  R2 = Resistor [tolerance=±5% resistance=22 package="0603 [SMD]"]
  C2 = Electrolytic Capacitor [capacitance=4.7µF voltage=35V package="0807 [SMD, electrolytic]"]
  C4 = Ceramic Capacitor [capacitance="100 nF" voltage=35V package="1206 [SMD, multilayer]"]
  Debugger1 = Debugger

nets:
  N1: M1.A9, Debugger1.RX
  N2: M1.A10, Debugger1.TX
  GND: M1.G, M1.GND, U1.GND, C2.-, C4.0, Debugger1.GND
  3.3V: M1.3.3V, U1.VCC, C2.+, C4.1
  N3: M1.A2, U1.DI
  N4: M1.A3, U1.RO
  N5: M1.A5, U1.RE, U1.DE
  N6: U1.A, R2.Pin_0
  N7: U1.B, R1.Pin_1
  N8: R1.Pin_0, R2.Pin_1

notes:
  3.3V transceiver needed instead of MAX485: ADM3485E or SN65HVD12
  RS-485 B A
